// Logisim project ALU-final.circ as structural Verilog: 1 circuit, main circuit Overflow
// as
module Overflow (
  input  MSB,
  input  in_2,
  input  in_3,
  input  LSB,
  input  [31:0] _32_bit_INPUT,
  output [31:0] _32_bit_OUTPUT_CURRENT
);

  wire adder_1_cout, CLK_out, comparator_1_eq, ERR_out, ERROR_q, RST_out;
  wire [31:0] adder_1_out, AND_out, divider_1_out, divider_1_rem, multiplexer_1_out, multiplier_1_out,
       NAND_out, NOR_out, NOT_out, OR_out, shifter_1_out, shifter_2_out, subtractor_1_out, XNOR_out, XOR_out;

  Adder #(.width(32)) adder_1 (
    .a(_32_bit_OUTPUT_CURRENT), .b(_32_bit_INPUT), .out(adder_1_out), .cout(adder_1_cout));  // open: cin
  Subtractor #(.width(32)) subtractor_1 (
    .a(_32_bit_OUTPUT_CURRENT), .b(_32_bit_INPUT), .out(subtractor_1_out));  // open: bin, bout
  Multiplier #(.width(32)) multiplier_1 (
    .a(_32_bit_OUTPUT_CURRENT), .b(_32_bit_INPUT), .out(multiplier_1_out));  // open: cin, cout
  Divider #(.width(32)) divider_1 (
    .a(_32_bit_OUTPUT_CURRENT), .b(_32_bit_INPUT), .out(divider_1_out), .rem(divider_1_rem));  // open: upper
  Comparator #(.width(32)) comparator_1 (.a(_32_bit_INPUT), .b({32{1'b0}}), .eq(comparator_1_eq));  // open: gt, lt
  or ERR (ERR_out, adder_1_cout, comparator_1_eq);
  Clock CLK (.out(CLK_out));
  Register #(.width(32)) ACC (
    .D(multiplexer_1_out), .Q(_32_bit_OUTPUT_CURRENT), .clk(CLK_out), .clr(RST_out));  // open: en
  Multiplexer #(.select(4), .width(32), .enable("false")) multiplexer_1 (
    .in0(_32_bit_OUTPUT_CURRENT), .in1(adder_1_out), .in2(subtractor_1_out), .in3(multiplier_1_out),
    .in4(divider_1_out), .in5(divider_1_rem), .in6(AND_out), .in7(OR_out), .in8(XOR_out), .in9(NOT_out),
    .in10(NAND_out), .in11(NOR_out), .in12(XNOR_out), .in13(shifter_1_out), .in14(shifter_2_out),
    .in15({32{1'b0}}), .out(multiplexer_1_out), .sel({MSB, in_2, in_3, LSB}));
  Button RST (.out(RST_out));
  LED ERR_2 (.in(ERROR_q));
  assign XNOR_out = ~(_32_bit_OUTPUT_CURRENT ^ _32_bit_INPUT);  // XNOR_Gate XNOR, 32 bits wide
  assign NOR_out = ~(_32_bit_OUTPUT_CURRENT | _32_bit_INPUT);  // NOR_Gate NOR, 32 bits wide
  assign NAND_out = ~(_32_bit_OUTPUT_CURRENT & _32_bit_INPUT);  // NAND_Gate NAND, 32 bits wide
  assign NOT_out = ~_32_bit_OUTPUT_CURRENT;  // NOT_Gate NOT, 32 bits wide
  assign XOR_out = _32_bit_OUTPUT_CURRENT ^ _32_bit_INPUT;  // XOR_Gate XOR, 32 bits wide
  assign OR_out = _32_bit_OUTPUT_CURRENT | _32_bit_INPUT;  // OR_Gate OR, 32 bits wide
  assign AND_out = _32_bit_OUTPUT_CURRENT & _32_bit_INPUT;  // AND_Gate AND, 32 bits wide
  Shifter #(.width(32)) shifter_1 (.in(_32_bit_INPUT), .\dist (5'b00001), .out(shifter_1_out));
  D_Flip_Flop ERROR (.clk(CLK_out), .D(ERR_out), .Q(ERROR_q), .reset(RST_out));  // open: Qn, preset, en
  Shifter #(.width(32), .shift("lr")) shifter_2 (.in(_32_bit_INPUT), .\dist (5'b00001), .out(shifter_2_out));

  // Notes on the sheet:
  //   0001: ADD
  //   0010: SUB
  //   0011: MUL
  //   0100: DIV
  //   0101: MOD
  //   OP-CODE TABLE
  //   0000: no-operation
  //   S
  //   A
  //   Out
  //   B
  //   A
  //   Out
  //   B
  //   A
  //   Out
  //   B
  //   A
  //   Out
  //   B
  //   A
  //   B
  //   Error Check
  //   32-bits (0)
  //   ERR - OR gate:
  //   1 if Overflow or Div-by-0
  //   0110: AND
  //   0111: OR
  //   1000: XOR
  //   1001: NOT
  //   1010: NAND
  //   1011: NOR
  //   1100: XNOR
  //   OP-CODE INPUT
  //   D
  //   1101: SHL-logic
  //   1110: SHR-logic
  //   1111: RESET
  //   Q
  //   32-bit Register
  //   Out
  //   A
  //   B
  //   5-bits (01)
  //   Shift 1-bit 
  //   Error Check:
  //   • Divide-by-Zero (ACC/Input)
  //   32-bit Input == Low
  //   RED if(Input) == Low
  //   • Overflow
  //   32-bit Adder Overflow
  //   Out
  //   SHL
  //   A
  //   B
  //   SHR
  //   RED if(ACC+Input) == Overflow
  //   Out
endmodule
